# Fritzing sketch Circuit (saved by Fritzing 0.9.5d)
breadboards: 1

parts:
  M1 = DOIT Esp32 DevKit v1 (30 pins long, 11 pins width) [part_number=ESP32S-PIN30]
  LED1 = smd LED [color="Red (633nm)" package="1206 [SMD]"]
  R1 = Resistor [tolerance=±5% resistance=220 package="2010 [SMD]"]
  U1 = 4-Channel 5v Relay Shield [package=relay-4ch5v10a]
  Part1 = I2C level shifter bidirectional
  D1 = Rectifier Diode [part_number=1N4001 package="300 mil [THT]"]  # not connected
  Part3 = Adafruit ADS1015 12Bit I2C ADC [part_number="Adafruit #1083"]

nets:
  N1: M1.3V3, Part1.LV
  GND: M1.GND, LED1.cathode, U1.GND, Part1.GND, Part3.GND
  N2: M1.D21, Part3.SDA
  N3: M1.D22, Part3.SCL
  N4: M1.D33, R1.Pin_0
  N5: M1.D25, Part1.LV4
  N6: M1.D26, Part1.LV3
  N7: M1.D27, Part1.LV2
  N8: M1.D14, Part1.LV1
  N9: LED1.anode, R1.Pin_1
  VCC: U1.VCC, Part1.HV, Part3.VDD
  N10: U1.IN1, Part1.HV1
  N11: U1.IN2, Part1.HV2
  N12: U1.K1-In, U1.K3-In
  N13: U1.K1-Off, U1.K2-Off
  N14: U1.K2-In, U1.K4-In
  N15: U1.IN4, Part1.HV4
  N16: U1.IN3, Part1.HV3

notes:
  12V/24V Source
  2x Analog Inputs
  2x Digital Inputs
  HWT906-TTL
  1405 MLD

custom parts:
  DOIT Esp32 DevKit v1 (30 pins long, 11 pins width): The DOIT Esp32 DevKit v1 is one of the development board created by DOIT to evaluate the ESP-WROOM-32 module. It is based on the ESP32 microcontroller that boasts Wifi, Bluetooth, Ethernet and Low Power support all in a single chip. (vanepp) made breadboard work, adjusted pin numbering and labels and reduced size of schematic and cleaned up pcb. This chip is 30pins long (2 x15) and 11 pins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
  4-Channel 5v Relay Shield: 4 Channel 5v Relay Shield w. 2x SPD-06VDC-SD-C
  Adafruit ADS1015 12Bit I2C ADC: For microcontrollers without an analog-to-digital converter or when you want a higher-precision ADC, the ADS1015 provides 12-bit precision at 3300 samples/second over I2C. The chip can be configured as 4 single-ended input channels, or two differential channels. As a nice bonus, it even includes a programmable gain amplifier, up to x16, to help boost up smaller single/differential signals to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
